# Fritzing sketch Schematic (saved by Fritzing 0.9.3b)
perfboards: 2

parts:
  J1 = Power Jack [package=power_jack_pth]
  U1 = LM2596 step down module
  U2 = LM2596 step down module
  WeMos_D1_Mini1 = WeMos D1 Mini
  X1 = USB Connectors [package=usb-a-s]
  S1 = Toggle Switch [package=THT]
  Mod1 = OLED Mono 0.56 inch blue or white
  Part1 = ACS712 Low Current Sensor Board v12
  F1 = Fan - Ventilador [package=THT]
  R1 = Resistor [tolerance=±5% resistance=1k package=THT]
  LED1 = smd LED [color="Blue (470nm)" package="0603 [SMD]"]

nets (from the breadboard view):
  GND: J1.GND, U1.IN-, U1.OUT-, U2.IN-, U2.OUT-, WeMos_D1_Mini1.G, X1.GND, Mod1.GND, Part1.GND, F1.GND, LED1.cathode
  N1: J1.PWR, U1.IN+, U2.IN+
  N2: U1.OUT+, U2.OUT+, Part1.IP-
  5V: WeMos_D1_Mini1.5V, X1.VBUS, S1.L1, Part1.IP+, F1.5V, R1.Pin_1
  N3: WeMos_D1_Mini1.A0, Part1.VO
  N4: WeMos_D1_Mini1.D1, Mod1.SCL
  N5: WeMos_D1_Mini1.D2, Mod1.SDA
  N6: S1.COM, Mod1.VCC
  N7: R1.Pin_0, LED1.anode

custom parts:
  LM2596 step down module: LM2596 DC-DC step down power supply module 3 A.
  OLED Mono 0.56 inch blue or white: OLED, I2C 3.3V - 5V Blue and White text versions
  Fan - Ventilador: Ventilador de 2 pines, se encuentra comunmente en computadoras de escritorio
